# Fritzing sketch Project Circuit (saved by Fritzing 0.9.4)
breadboards: 1

parts:
  HC-SR04_Sensor_1 = HC-SR04 Ultrasonic Distance Sensor
  LED1 = RGB LED (com. cathode, rgb) [package="5 mm [THT]"]
  U1 = POT [package=pot_mammoth]
  J1 = Basic Servo
  Part1 = Arduino Uno (Rev3) - ICSP

nets:
  VCC: HC-SR04_Sensor_1.VCC, U1.A, J1.vcc, Part1.5V
  N1: HC-SR04_Sensor_1.TRIG, Part1.D10_PWM/SS
  GND: HC-SR04_Sensor_1.ECHO, U1.E, J1.gnd, Part1.GND
  N2: HC-SR04_Sensor_1.GND, Part1.D9_PWM
  N3: LED1.red_anode, Part1.D3_PWM
  N4: LED1.common_cathode, U1.S
  N5: LED1.green_anode, Part1.D2
  N6: J1.pulse, Part1.D8
